// Logisim project Bird.circ as structural Verilog
module Control_Unit (
  input  [3:0] in_1,
  output [8:0] out_2
);

  ROM #(.addrWidth(4), .dataWidth(9)) rom_1 (.addr(in_1), .data(out_2));  // open: sel

  // Other names for the same wires on the sheet: irld = out_2[0]; memld = out_2[1]; mux = out_2[2]; zfld = out_2[3];
  //   regld = out_2[4]; armux = out_2[5]; pcinc = out_2[6]; pcld = out_2[7]; fetch = out_2[8]

  // Notes on the sheet:
  //   Control Unit for Reptile     -      Including LD, ST, JUMP, JZ
  //   contents of rom_1 (hex, n*v repeats v):
  //   141 51 34 22 0 80 0 18
endmodule

module ALU (
  input  [15:0] A,
  input  [15:0] B,
  input  [5:0] AluOp,
  output [15:0] AluResult,
  output Zero
);

  wire [15:0] adder_1_out, adder_2_out, Bitwise_And_out, Bitwise_Not_out, Bitwise_Or_out, Bitwise_Xor_out,
       multiplexer_1_out, subtractor_1_out, subtractor_2_out;

  assign Bitwise_And_out = A & B;  // AND_Gate Bitwise_And, 16 bits wide
  assign Bitwise_Or_out = A | B;  // OR_Gate Bitwise_Or, 16 bits wide
  assign Bitwise_Xor_out = A ^ B;  // XOR_Gate Bitwise_Xor, 16 bits wide
  assign Bitwise_Not_out = ~B;  // NOT_Gate Bitwise_Not, 16 bits wide
  Adder #(.width(16)) adder_1 (.a(A), .b(B), .out(adder_1_out));  // open: cin, cout
  Subtractor #(.width(16)) subtractor_1 (.a(A), .b(B), .out(subtractor_1_out));  // open: bin, bout
  Adder #(.width(16)) adder_2 (.a(B), .b(16'h1), .out(adder_2_out));  // open: cin, cout
  Subtractor #(.width(16)) subtractor_2 (.a(B), .b(16'h1), .out(subtractor_2_out));  // open: bin, bout
  Multiplexer #(.select(2), .width(16)) multiplexer_1 (
    .in0(Bitwise_Not_out), .in1(B), .in2(adder_2_out), .in3(subtractor_2_out), .out(multiplexer_1_out),
    .sel(AluOp[1:0]));  // open: en
  Multiplexer #(.select(3), .width(16)) multiplexer_2 (
    .in0(adder_1_out), .in1(subtractor_1_out), .in2(Bitwise_And_out), .in3(Bitwise_Or_out),
    .in4(Bitwise_Xor_out), .in7(multiplexer_1_out), .out(AluResult), .sel(AluOp[5:3]));  // open: in5, in6, en
  nor nor_1 (Zero, AluResult[0], AluResult[1], AluResult[2], AluResult[3], AluResult[4], AluResult[5], AluResult[6], AluResult[7], AluResult[9], AluResult[10], AluResult[11], AluResult[12], AluResult[13], AluResult[14], AluResult[15], AluResult[8]);

  // Notes on the sheet:
  //   Adder
  //   Substractor
  //   Move
endmodule

module RegBank (
  input  in_1,
  input  in_2,
  output out_3
);

  wire clock_1_out;

  Clock clock_1 (.out(clock_1_out));
  S_R_Flip_Flop s_r_ff_1 (.S(in_1), .R(in_2), .Q(out_3), .preset(clock_1_out));  // open: clk, Qn, reset, en
endmodule

module _1_bit_Register (
  input  Data,
  input  Load,
  input  clk,
  output Output
);

  wire and_1_out, and_2_out, not_1_out;

  and and_1 (and_1_out, Data, Load);
  not not_1 (not_1_out, Data);
  and and_2 (and_2_out, not_1_out, Load);
  S_R_Flip_Flop s_r_ff_1 (.S(and_1_out), .clk(clk), .R(and_2_out), .Q(Output));  // open: Qn, preset, reset, en
endmodule
